# Fritzing sketch BUS (saved by Fritzing 1.0.1rc)

parts:
  MCU1 = Wemos Lolin32lite
  L298N1 = L298N DC motor driver
  A1 = OKY3513
  A2 = OKY3513
  A3 = OKY3513

nets:
  N1: MCU1.pin_6, L298N1.ENB
  N2: MCU1.pin_7, L298N1.IN4
  N3: MCU1.pin_8, L298N1.IN3
  N4: MCU1.pin_9, L298N1.IN2
  N5: MCU1.pin_10, L298N1.IN1
  N6: MCU1.pin_11, L298N1.ENA
  N7: MCU1.pin_13, A1.Pin_1, A2.Pin_1, A3.Pin_1
  N8: MCU1.pin_23, A1.Pin_3
  N9: MCU1.pin_24, A2.Pin_3
  N10: MCU1.pin_25, A3.Pin_3
  N11: MCU1.pin_28, A1.Pin_2, A2.Pin_2, A3.Pin_2

custom parts:
  Wemos Lolin32lite: Wemos Lolinlite32 wifi and blue tooth board based on the ESP-32 cpu, digital I/Os 19, analog inputs 6, clock 240mhz, Flash 4Mbytes, lipo battery charger (500ma connection broken out on breadboard but not pcb), usb.
  L298N DC motor driver: 2x DC motor driver with 78M05 positive voltage regulator (7..35 V) L298N: max 46 V, 2 A Set 5 V Enable jumper to enable 5 V regultor (needed for the L298N) and +5 V output at screw terminal or supply external +5 V at screw terminal Set ENA and/or ENB to +5 V to enable motor permanently or supply ENA and/or ENB with PWM signal IN1 and IN2 set rotation directory for motor A (OUT1/OUT2) IN2 and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
  OKY3513: TCRT5000 IR Infrared Sensor Line Tracker Sensor Obstacle Avoidance Module.
