# Fritzing sketch sketch (saved by Fritzing 0.9.3b)

parts:
  A2 = Esp32-c3 super mini
  LED1 = LED - 3mm [color="Yellow (595nm)" package="3 mm [THT]"]
  LED2 = LED - 3mm [color="Green (570nm)" package="3 mm [THT]"]
  LED3 = LED - 3mm [color="Red (633nm)" package="3 mm [THT]"]
  Mod1 = KY-005 Infrared Transmitter Module [package="Breakout board"]

nets:
  N1: A2.Pin_1, Mod1.S
  N2: A2.Pin_10, LED2.anode
  N3: A2.Pin_11, LED1.anode
  N4: A2.Pin_12, LED3.anode
  N5: A2.Pin_15, LED1.cathode, LED2.cathode, LED3.cathode, Mod1.-
  N6: A2.Pin_16, Mod1.Vin

custom parts:
  Esp32-c3 super mini: ESP32-C3 Development Board ESP32 SuperMini Development Board ESP32 Development Board WiFi Bluetooth.
  KY-005 Infrared Transmitter Module: Arduino IR Transmitter Module Keyes KY-005, emits infrared light at 38KHz.
